// Logisim project lab2_mux_task3.circ as structural Verilog: 1 circuit, main circuit main
module main (
  input  y0,
  input  y1,
  input  y2,
  input  y3,
  input  y4,
  input  y5,
  input  y6,
  input  y7,
  input  c,
  input  b,
  input  a,
  output out_12
);

  wire and_1_out, and_2_out, and_3_out, and_4_out, and_5_out, and_6_out, and_7_out, and_8_out, not_1_out,
       not_2_out, not_3_out;

  not not_1 (not_1_out, c);
  not not_2 (not_2_out, a);
  not not_3 (not_3_out, b);
  and and_1 (and_1_out, not_1_out, y0, not_3_out, not_2_out);
  and and_2 (and_2_out, y1, not_2_out, not_3_out, c);
  and and_3 (and_3_out, not_2_out, b, b, not_1_out, y2);
  and and_4 (and_4_out, not_2_out, y3, b, c);
  and and_5 (and_5_out, a, y4, not_3_out, not_1_out);
  and and_6 (and_6_out, a, y5, not_3_out, c);
  and and_7 (and_7_out, a, y6, b, not_1_out);
  and and_8 (and_8_out, c, y7, a, b);
  or or_1 (out_12, and_1_out, and_2_out, and_3_out, and_4_out, and_5_out, and_6_out, and_7_out, and_8_out);
endmodule
