// Logisim project alu32bit.circ as structural Verilog: 1 circuit, main circuit main
module main (
  input  [31:0] in_1,
  input  in_2,
  input  [31:0] in_3,
  input  [3:0] in_4,
  input  in_5,
  output out_6,
  output [31:0] out_7
);

  wire comparator_1_gt;
  wire [31:0] adder_1_out, and_1_out, bit_extender_1_out, bit_extender_2_out, or_1_out, shifter_1_out,
       shifter_2_out, shifter_3_out, subtractor_1_out, xor_1_out;

  Shifter #(.width(32)) shifter_1 (.in(in_1), .\dist (in_3[4:0]), .out(shifter_1_out));
  Shifter #(.width(32), .shift("lr")) shifter_2 (.in(in_1), .\dist (in_3[4:0]), .out(shifter_2_out));
  Shifter #(.width(32), .shift("ar")) shifter_3 (.in(in_1), .\dist (in_3[4:0]), .out(shifter_3_out));
  Comparator #(.width(32), .mode("unsigned")) comparator_1 (.a(in_1), .b(in_3), .gt(comparator_1_gt));  // open: eq, lt
  Adder #(.width(32)) adder_1 (.a(in_1), .b(in_3), .out(adder_1_out), .cin(in_2), .cout(out_6));
  assign and_1_out = in_1 & in_3;  // AND_Gate and_1, 32 bits wide
  assign or_1_out = in_1 | in_3;  // OR_Gate or_1, 32 bits wide
  assign xor_1_out = in_1 ^ in_3;  // XOR_Gate xor_1, 32 bits wide
  Subtractor #(.width(32)) subtractor_1 (.a(in_1), .b(in_3), .out(subtractor_1_out));  // open: bin, bout
  assign bit_extender_1_out = {{31{1'b0}}, comparator_1_gt};  // Bit_Extender bit_extender_1
  assign bit_extender_2_out = {{31{1'b0}}, in_5};  // Bit_Extender bit_extender_2
  Multiplexer #(.select(4), .width(32), .enable("false")) multiplexer_1 (
    .in0(adder_1_out), .in1(subtractor_1_out), .in2(and_1_out), .in3(or_1_out), .in4(xor_1_out),
    .in5(bit_extender_1_out), .in6(shifter_1_out), .in7(shifter_2_out), .in8(shifter_3_out),
    .in9(bit_extender_2_out), .in10(bit_extender_2_out), .in11(bit_extender_2_out),
    .in12(bit_extender_2_out), .in13(bit_extender_2_out), .in14(bit_extender_2_out),
    .in15(bit_extender_2_out), .out(out_7), .sel(in_4));

  // Notes on the sheet:
  //   A
  //   B
  //   ALU Operation
endmodule
